# Fritzing sketch serverraumüberwachung (saved by Fritzing 1.0.1rc)
breadboards: 1

parts:
  Part1 = Arduino Mega ADK (Rev3)
  HC-SR04_Sensor_1 = HC-SR04 Ultrasonic Distance Sensor
  T1 = TMP36 Temperature Sensor [package="TO92 [THT]"]

nets:
  N1: Part1.A0, T1.Vout
  5V: Part1.5V, HC-SR04_Sensor_1.VCC, T1.+Vs
  GND: Part1.GND, HC-SR04_Sensor_1.GND, T1.GND
  N2: Part1.D3_PWM, HC-SR04_Sensor_1.TRIG
  N3: Part1.D4_PWM, HC-SR04_Sensor_1.ECHO
